// Logisim project binaryaddition.circ as structural Verilog: 3 circuits, main circuit main
module main (
  input  in_1,
  input  in_2,
  input  in_3,
  input  in_4,
  input  in_5,
  input  in_6,
  input  in_7,
  input  in_8,
  input  in_9,
  input  in_10,
  input  in_11,
  input  in_12,
  input  in_13,
  input  in_14,
  input  in_15,
  input  in_16,
  output overflow,
  output out_18,
  output out_19,
  output out_20,
  output out_21,
  output out_22,
  output out_23,
  output out_24,
  output out_25
);

  wire fulladder_2_carryout, fulladder_3_carryout, fulladder_4_carryout, fulladder_5_carryout,
       fulladder_6_carryout, fulladder_7_carryout, halfadder_1_carry;

  fulladder fulladder_1 (.carryin(fulladder_2_carryout), .A(in_2), .B(in_3), .sum(out_21), .carryout(overflow));
  fulladder fulladder_2 (
    .carryin(fulladder_3_carryout), .A(in_7), .B(in_8), .sum(out_18), .carryout(fulladder_2_carryout));
  fulladder fulladder_3 (
    .carryin(fulladder_4_carryout), .A(in_11), .B(in_12), .sum(out_19), .carryout(fulladder_3_carryout));
  fulladder fulladder_4 (
    .carryin(fulladder_5_carryout), .A(in_13), .B(in_14), .sum(out_20), .carryout(fulladder_4_carryout));
  fulladder fulladder_5 (
    .carryin(fulladder_6_carryout), .A(in_16), .B(in_15), .sum(out_22), .carryout(fulladder_5_carryout));
  fulladder fulladder_6 (
    .carryin(fulladder_7_carryout), .A(in_6), .B(in_4), .sum(out_24), .carryout(fulladder_6_carryout));
  fulladder fulladder_7 (
    .carryin(halfadder_1_carry), .A(in_9), .B(in_5), .sum(out_23), .carryout(fulladder_7_carryout));
  halfadder halfadder_1 (.A(in_10), .B(in_1), .Carry(halfadder_1_carry), .Sum(out_25));
endmodule

module halfadder (
  input  A,
  input  B,
  output Carry,
  output Sum
);

  and and_1 (Carry, A, B);
  xor xor_1 (Sum, A, B);
endmodule

module fulladder (
  input  carryin,
  input  A,
  input  B,
  output sum,
  output carryout
);

  wire and_1_out, and_2_out, xor_1_out;

  xor xor_1 (xor_1_out, A, B);
  and and_1 (and_1_out, A, B);
  xor xor_2 (sum, carryin, xor_1_out);
  and and_2 (and_2_out, carryin, xor_1_out);
  or or_1 (carryout, and_2_out, and_1_out);
endmodule
