// Logisim project logiccircuitquestions.circ as structural Verilog: 1 circuit, main circuit main
module main (
  input  in_1,
  input  in_2,
  input  in_3,
  input  in_4,
  input  in_5,
  input  in_6,
  input  in_7,
  output out_8,
  output out_9,
  output out_10
);

  wire and_1_out, not_1_out, not_2_out;

  not not_1 (not_1_out, in_4);
  not not_2 (not_2_out, in_7);
  and and_1 (and_1_out, in_5, in_6);
  or or_1 (out_8, in_1, in_2);
  and and_2 (out_9, in_3, not_1_out);
  and and_3 (out_10, and_1_out, not_2_out);
endmodule
